# Fritzing sketch lightphone (saved by Fritzing 0.9.2b)
breadboards: 1

parts:
  U1 = MCP6004 - Low Power, rail-to-rail Quad Operational Amplifier [part_number=MCP6004]
  VCC1 = 4 x AAA Battery Mount
  R1 = Trimmer Potentiometer [maximum_resistance=1MΩ package=THT]
  R2 = Trimmer Potentiometer [maximum_resistance=1MΩ package=THT]
  R3 = Trimmer Potentiometer [maximum_resistance=1MΩ package=THT]
  Mic_(sleeve) = female pin header, 1 pin [form="♀ (female)"]
  Left_(tip) = female pin header, 1 pin [form="♀ (female)"]
  Gnd_(ring_2) = female pin header, 1 pin [form="♀ (female)"]
  Right_(ring_1) = female pin header, 1 pin [form="♀ (female)"]
  C1 = Ceramic Capacitor [capacitance="100 nF" package="0603 [SMD, multilayer]"]
  C2 = Ceramic Capacitor [capacitance="100 nF" package="0603 [SMD, multilayer]"]
  R4 = Resistor [tolerance=±5% resistance=1k package=THT]
  C3 = Ceramic Capacitor [capacitance=1nF package="200 mil [THT, multilayer]"]
  Q1 = NPN-Transistor [package="TO92 [THT]"]
  R5 = Resistor [tolerance=±5% resistance=220 package=THT]
  R6 = Resistor [tolerance=±5% resistance=100k package=THT]
  R7 = Resistor [tolerance=±5% resistance=47k package=THT]
  R8 = Resistor [tolerance=±5% resistance=47k package=THT]
  R9 = Resistor [tolerance=±5% resistance=47k package=THT]
  R10 = Resistor [tolerance=±5% resistance=47k package=THT]
  R11 = Resistor [tolerance=±5% resistance=100k package=THT]
  J1 = female pin header, 2 pins [form="♀ (female)"]  # not connected
  Q2 = LTR-301 [part_number=BPW40 package=ltr-301]
  R12 = Resistor [tolerance=±5% resistance=47k package=THT]
  J2 = female pin header, 2 pins [form="♀ (female)"]  # not connected
  LED1 = smd LED [color="White (4500K)" package="0805 [SMD]"]
  R13 = Resistor [tolerance=±5% resistance=1k package=THT]

nets:
  N1: U1.OUTA, R13.Pin_0
  N2: U1.-INA, Left_(tip).pin1
  N3: U1.+INA, Right_(ring_1).pin1
  N4: U1.V+, VCC1.+, R1.leg2, R2.leg2, R12.Pin_0
  N5: U1.+INB, R9.Pin_1, R11.Pin_1, Q2.C, R12.Pin_1
  N6: U1.-INB, R2.wiper
  N7: U1.OUTC, U1.-IND, R3.leg2, C3.1, R7.Pin_1
  N8: U1.-INC, C3.0, R10.Pin_0, R11.Pin_0
  N9: U1.+INC, R8.Pin_0, R9.Pin_0
  N10: U1.V-, VCC1.-, R1.leg1, R2.leg1, R3.leg1, C1.0, Q1.C, R8.Pin_1, Q2.E, LED1.cathode
  N11: U1.+IND, R6.Pin_1
  N12: U1.OUTD, R5.Pin_1, R6.Pin_0
  N13: R1.wiper, Gnd_(ring_2).pin1, C1.1, R4.Pin_1, R7.Pin_0
  N14: R3.wiper, C2.0
  N15: Mic_(sleeve).pin1, C2.1, R4.Pin_0
  N16: Q1.E, R10.Pin_1
  N17: Q1.B, R5.Pin_0
  N18: LED1.anode, R13.Pin_1
